# Fritzing sketch Speedy (saved by Fritzing 0.9.3b)
breadboards: 1

parts:
  Part1 = Arduino Mega 2560 (Rev3)
  M1 = DC Motor
  hc-sr1 = hc-sr04
  M2 = DC Motor
  Part2 = Bluetooth HC-05 Macho
  S2 = H-Bridge with L298N
  M3 = DC Motor
  M4 = DC Motor
  VCC2 = Battery
  S1 = H-Bridge with L298N
  VCC3 = Battery
  J1 = Basic Servo  # not connected

nets:
  N1: Part1.D19/RX1, Part2.TXD
  N2: Part1.D18/TX1, Part2.RXD
  3V3: Part1.3V3, Part2.VCC
  5V: Part1.5V, S2.5V
  GND: Part1.GND, hc-sr1.GND, Part2.GND, S2.GND, S1.GND, VCC3.-
  N3: Part1.D2_PWM, S2.ENA
  N4: Part1.D3_PWM, S2.ENB
  N5: Part1.D4_PWM, S1.ENA
  N6: Part1.D5_PWM, S1.ENB
  N7: Part1.D44, hc-sr1.Echo
  N8: Part1.D45, hc-sr1.Trig
  N9: Part1.D46, S1.IN4
  N10: Part1.D47, S1.IN3
  N11: Part1.D48, S1.IN2
  N12: Part1.D49, S1.IN1
  N13: Part1.D50, S2.IN3
  N14: Part1.D51, S2.IN4
  N15: Part1.D52, S2.IN1
  N16: Part1.D53, S2.IN2
  N17: M1.pin_1, S1.M2-01
  N18: M1.pin_2, S1.M2-02
  VCC: hc-sr1.VCC, S1.5V
  N19: M2.pin_1, S1.M1-02
  N20: M2.pin_2, S1.M1-01
  N21: S2.12V, VCC2.+
  N22: S2.M1-01, M4.pin_1
  N23: S2.M1-02, M4.pin_2
  N24: S2.M2-01, M3.pin_2
  N25: S2.M2-02, M3.pin_1
  N26: S1.12V, VCC3.+

notes:
  remove ena and enb jumper
  pins:
  2 driver left ena
  3 driver left enb
  4 driver right ena
  5 driver right enb
  52 driver left in1
  53 driver left in2
  50 driver left in3
  51 driver left in4
  49 driver right in1
  48 driver right in2
  47 driver right in3
  46 driver right in4
  45 hc-sr04 trig
  44 hc-sr04 echo
  3v3 hc05 vcc
  rx1 hc05 tx1
  tx1 hc05 rx1
  a0 servo

custom parts:
  H-Bridge with L298N: h-bridge
